// Logisim project 4bit AdderSubber 2 screen.circ as structural Verilog: 1 circuit, main circuit main
module main (
  input  in_1,
  input  in_2,
  input  in_3,
  input  in_4,
  input  in_5,
  input  in_6,
  input  in_7,
  input  in_8,
  input  in_9
);

  wire and_1_out, and_2_out, and_3_out, and_4_out, and_5_out, and_6_out, and_7_out, and_8_out, and_9_out,
       and_10_out, and_11_out, and_12_out, and_13_out, and_14_out, and_15_out, and_16_out, and_17_out,
       and_18_out, not_1_out, not_2_out, or_1_out, or_2_out, or_3_out, or_4_out, or_5_out, or_6_out,
       or_7_out, xor_1_out, xor_2_out, xor_3_out, xor_4_out, xor_5_out, xor_6_out, xor_7_out, xor_8_out,
       xor_9_out, xor_10_out, xor_11_out, xor_12_out, xor_13_out, xor_14_out, xor_15_out, xor_16_out,
       xor_17_out, xor_18_out, xor_19_out, xor_20_out;
  wire [3:0] xor_21_out;

  _7_Segment_Display u_7_segment_display_1 (.g(and_10_out), .b(and_1_out), .c(and_1_out));  // open: f, a, e, d, dp
  Hex_Digit_Display hex_digit_display_1 (.value(xor_21_out));  // open: dp
  xor xor_1 (xor_1_out, in_9, in_1);
  xor xor_2 (xor_2_out, in_8, in_1);
  xor xor_3 (xor_3_out, in_7, in_1);
  xor xor_4 (xor_4_out, in_6, in_1);
  and and_1 (and_1_out, or_4_out, not_1_out);
  xor xor_5 (xor_5_out, in_5, xor_1_out);
  xor xor_6 (xor_6_out, in_4, xor_2_out);
  xor xor_7 (xor_7_out, in_3, xor_3_out);
  xor xor_8 (xor_8_out, in_2, xor_4_out);
  not not_1 (not_1_out, in_1);
  xor xor_9 (xor_9_out, in_1, xor_5_out);
  xor xor_10 (xor_10_out, or_1_out, xor_6_out);
  xor xor_11 (xor_11_out, or_2_out, xor_7_out);
  xor xor_12 (xor_12_out, or_3_out, xor_8_out);
  and and_2 (and_2_out, xor_5_out, in_1);
  and and_3 (and_3_out, in_5, xor_1_out);
  and and_4 (and_4_out, xor_6_out, or_1_out);
  and and_5 (and_5_out, in_4, xor_2_out);
  and and_6 (and_6_out, xor_7_out, or_2_out);
  and and_7 (and_7_out, in_3, xor_3_out);
  and and_8 (and_8_out, xor_8_out, or_3_out);
  and and_9 (and_9_out, in_2, xor_4_out);
  or or_1 (or_1_out, and_2_out, and_3_out);
  or or_2 (or_2_out, and_4_out, and_5_out);
  or or_3 (or_3_out, and_6_out, and_7_out);
  or or_4 (or_4_out, and_8_out, and_9_out);
  not not_2 (not_2_out, or_4_out);
  and and_10 (and_10_out, in_1, not_2_out);
  xor xor_13 (xor_13_out, xor_9_out, and_10_out);
  xor xor_14 (xor_14_out, xor_10_out, and_10_out);
  xor xor_15 (xor_15_out, xor_11_out, and_10_out);
  xor xor_16 (xor_16_out, xor_12_out, and_10_out);
  xor xor_17 (xor_17_out, 1'b0, xor_13_out);
  xor xor_18 (xor_18_out, 1'b0, xor_14_out);
  xor xor_19 (xor_19_out, 1'b0, xor_15_out);
  xor xor_20 (xor_20_out, 1'b0, xor_16_out);
  xor xor_21 (xor_21_out[0], and_10_out, xor_17_out);
  xor xor_22 (xor_21_out[1], or_5_out, xor_18_out);
  xor xor_23 (xor_21_out[2], or_6_out, xor_19_out);
  xor xor_24 (xor_21_out[3], or_7_out, xor_20_out);
  and and_11 (and_11_out, xor_17_out, and_10_out);
  and and_12 (and_12_out, 1'b0, xor_13_out);
  and and_13 (and_13_out, xor_18_out, or_5_out);
  and and_14 (and_14_out, 1'b0, xor_14_out);
  and and_15 (and_15_out, xor_19_out, or_6_out);
  and and_16 (and_16_out, 1'b0, xor_15_out);
  and and_17 (and_17_out, xor_20_out, or_7_out);
  and and_18 (and_18_out, 1'b0, xor_16_out);
  or or_5 (or_5_out, and_11_out, and_12_out);
  or or_6 (or_6_out, and_13_out, and_14_out);
  or or_7 (or_7_out, and_15_out, and_16_out);
  // OR_Gate or_8 has open pins: in1=and_17_out, in3=and_18_out, out=open
endmodule
